// Logisim project cpu.circ as structural Verilog: 1 circuit, main circuit CPU
module CPU (
  input  [31:0] Instruction,
  input  CLK,
  output [31:0] s0,
  output [31:0] s1,
  output [31:0] t0,
  output [31:0] t1,
  output [31:0] a0,
  output [31:0] ra,
  output [31:0] sp,
  output [31:0] PC
);

  wire comparator_1_eq, comparator_2_eq, undriven, we;
  wire [3:0] op;
  wire [31:0] alu_1_out, data, imm, imm_b, imm_i, imm_j, imm_s, imm_u, incrementer_1_p2, regfile_1_r1;

  // Incrementer incrementer_1: pin names not known; wires that end beside it: PC, incrementer_1_p2
  PC pc_1 (.Input(incrementer_1_p2), .Clk(CLK), .Output(PC));
  RegFile regfile_1 (
    .Clk(CLK), .R1(regfile_1_r1), .WE(we), .W(data), .RD(Instruction[11:7]), .RS1(Instruction[19:15]),
    .RS2(Instruction[24:20]), .s0(s0), .s1(s1), .t0(t0), .t1(t1), .a0(a0), .ra(ra), .sp(sp));  // open: R2
  assign imm_i = {{20{Instruction[31]}}, Instruction[31:20]};  // Bit_Extender bit_extender_1
  Comparator #(.width(5)) comparator_1 (.a(Instruction[6:2]), .b(5'b01000), .eq(comparator_1_eq));  // open: gt, lt
  Comparator #(.width(5)) comparator_2 (.a(Instruction[6:2]), .b(5'b11000), .eq(comparator_2_eq));  // open: gt, lt
  assign imm_u = {{12{Instruction[31]}}, Instruction[31:12]};  // Bit_Extender bit_extender_2
  nor nor_1 (we, comparator_1_eq, comparator_2_eq);
  ALU alu_1 (.A(regfile_1_r1), .B(imm), .ALU_Op(op), .Out(alu_1_out));  // open: Equal, LT, LTU
  assign imm_s = {{20{Instruction[31]}}, {Instruction[31:25], Instruction[11:7]}};  // Bit_Extender bit_extender_3
  assign imm_b = {{20{Instruction[31]}}, {Instruction[31:25], Instruction[11:7]}};  // Bit_Extender bit_extender_4
  assign imm_j = {{12{Instruction[31]}}, Instruction[31:12]};  // Bit_Extender bit_extender_5
  memory_main main_1 (.Address(alu_1_out), .WE(undriven), .Clk(CLK));  // open: Data, Out
  Multiplexer #(.select(5), .width(4)) multiplexer_1 (
    .in0(4'b0010), .out(op), .sel({5{1'b0}}));  // open: in1, in2, in3, in4, in5, in6, in7, in8, in9, in10, in11, in12, in13, in14, in15, in16, in17, in18, in19, in20, in21, in22, in23, in24, in25, in26, in27, in28, in29, in30, in31, en
  Multiplexer #(.select(5), .width(32)) multiplexer_2 (
    .out(imm), .sel({5{1'b0}}));  // open: in0, in1, in2, in3, in4, in5, in6, in7, in8, in9, in10, in11, in12, in13, in14, in15, in16, in17, in18, in19, in20, in21, in22, in23, in24, in25, in26, in27, in28, in29, in30, in31, en

  // Other names for the same wires on the sheet: b_imm0_4[4:0] = Instruction[11:7]; INST[31:0] = Instruction;
  //   rd[4:0] = Instruction[11:7]; s_imm0_4[4:0] = Instruction[11:7]; func3[2:0] = Instruction[14:12];
  //   j_imm1_10[9:0] = Instruction[21:12]; j_imm12_31[19:0] = Instruction[31:12];
  //   u_imm12_31[19:0] = Instruction[31:12]; rs1[4:0] = Instruction[19:15]; rs2[4:0] = Instruction[24:20];
  //   j_imm11 = Instruction[22]; j_imm12_19[7:0] = Instruction[30:23]; b_imm5_11[6:0] = Instruction[31:25];
  //   func7[6:0] = Instruction[31:25]; s_imm5_11[6:0] = Instruction[31:25]; j_imm20 = Instruction[31];
  //   fetch_addr[31:0] = PC; opcode[4:0] = Instruction[6:2]

  // Notes on the sheet:
  //   3: bits 7-11 rd
  //   4: bits 15-19 rs1
  //   5: bits 20-23 rs2
  //   jtype
  //   0 (top) bits 2-6: opcode
  //   1: bits 12-14 func3
  //   2: bits 25-31 func7
  //   NOTE
  //   Please do not modify/replace/move/change/delete/etc input and output pins
  //   rtype
  //   itype
  //   stype
  //   btype
  //   utype
  //   Etos 4 campos vienen del CU
  //   Stype y Btype WE=false, de lo contrario True
  //   UNIDAD DE CONTROL
  //   R: 01100XX: 12
  //   I: 00100XX: 4
  //   S: 01000xx: 8 
  //   B: 11000xx: 24
  //   U:01101xx:13
  //   J:11011xx:27
  //   These are debug/test outputs from your circuit
  //   Aca deberia calcular un valor de opcode/func3/func7 para mandar un op al ALU.
  //   Dependiendo de Opcode selecciono uno de los inmmediatos calculaods
  //   Señal de control elegida, va a ALU
  //   Señal de control elegida, va a ALU
endmodule
